// Logisim project p-cpu.circ as structural Verilog
module p_gate_single (
  input  [31:0] iLane1,
  input  [31:0] iLane2,
  input  [31:0] iLane3,
  input  [31:0] iLane4,
  input  [31:0] iLane5,
  input  [31:0] ILane6,
  input  [31:0] iRegister,
  input  Clock,
  input  [63:0] Gate_Instruction,
  input  GateProgram,
  output [31:0] oLane1,
  output [31:0] oLane2,
  output [31:0] oLane3,
  output [31:0] oLane4,
  output [31:0] oLane5,
  output [31:0] oLane6,
  output [31:0] oRegister,
  output [2:0] RegisterSel,
  output RegisterClear
);

  wire LaneA_q, LaneB_q, LaneC_q;
  wire [2:0] Clear_q, LaneEN_q;
  wire [7:0] GateCode_GG_q;
  wire [10:0] GateTag_t11_q;
  wire [11:0] SrcA_q, SrcB_q, SrcC_q;

  Register GateCode_GG (.D(Gate_Instruction[7:0]), .en(1'b1), .clk(GateProgram), .Q(GateCode_GG_q));  // open: clr
  Register #(.width(1)) LaneA (.D(Gate_Instruction[20]), .en(1'b1), .clk(GateProgram), .Q(LaneA_q));  // open: clr
  Register #(.width(1)) LaneB (.D(Gate_Instruction[33]), .en(1'b1), .clk(GateProgram), .Q(LaneB_q));  // open: clr
  Register #(.width(1)) LaneC (.D(Gate_Instruction[46]), .en(1'b1), .clk(GateProgram), .Q(LaneC_q));  // open: clr
  Register #(.width(3)) LaneEN (.D(Gate_Instruction[52:50]), .en(1'b1), .clk(GateProgram), .Q(LaneEN_q));  // open: clr
  Register #(.width(12)) SrcA (.D(Gate_Instruction[19:8]), .en(1'b1), .clk(GateProgram), .Q(SrcA_q));  // open: clr
  Register #(.width(12)) SrcB (.D(Gate_Instruction[32:21]), .en(1'b1), .clk(GateProgram), .Q(SrcB_q));  // open: clr
  Register #(.width(12)) SrcC (.D(Gate_Instruction[45:34]), .en(1'b1), .clk(GateProgram), .Q(SrcC_q));  // open: clr
  Register #(.width(3)) Clear (.D(Gate_Instruction[49:47]), .en(1'b1), .clk(GateProgram), .Q(Clear_q));  // open: clr
  Register #(.width(11)) GateTag_t11 (
    .D(Gate_Instruction[63:53]), .en(1'b1), .clk(GateProgram), .Q(GateTag_t11_q));  // open: clr
  Register #(.width(32)) A (.clr(Clock));  // open: D, en, clk, Q
  Register #(.width(32)) B (.clr(Clock));  // open: D, en, clk, Q
endmodule

module register_block (
  input  Clear,
  input  Clock,
  input  [31:0] Data,
  input  [11:0] Register_Select,
  output [31:0] out_5
);

  wire and_1_out, and_2_out, and_3_out, and_4_out, and_5_out, and_6_out, and_7_out, and_8_out, and_9_out,
       and_10_out, and_11_out, and_12_out, and_13_out, and_14_out, and_15_out, and_16_out, and_17_out,
       and_18_out, and_19_out, and_20_out, and_21_out, and_22_out, and_23_out, and_24_out, and_25_out,
       and_26_out, and_27_out, and_28_out, and_29_out, and_30_out, and_31_out, and_32_out, and_33_out,
       and_34_out, and_35_out, and_36_out, and_37_out, and_38_out, and_39_out, and_40_out, and_41_out,
       and_42_out, and_43_out, and_44_out, and_45_out, and_46_out, and_47_out;
  wire [3:0] Arithmetic_Register_out, Control_Register_out, Plain_Register_out;
  wire [7:0] xnor_1_out, xnor_2_out, xnor_3_out, xnor_4_out, xnor_5_out, xnor_6_out, xnor_7_out, xnor_8_out,
       xnor_9_out, xnor_10_out, xnor_11_out, xnor_12_out, xnor_13_out, xnor_14_out, xnor_15_out, xnor_16_out,
       xnor_17_out, xnor_18_out, xnor_19_out, xnor_20_out, xnor_21_out, xnor_22_out;
  wire [31:0] maa_q, mab_q, mac_q, mad_q, mba_q, mbb_q, mbc_q, mbd_q, mca_q, mcb_q, mcc_q, mcd_q, mda_q,
       mdb_q, multiplexer_1_out, multiplexer_2_out, multiplexer_3_out, multiplexer_4_out, multiplexer_5_out,
       multiplexer_6_out, multiplexer_7_out, multiplexer_8_out, multiplexer_9_out, multiplexer_10_out,
       multiplexer_11_out, multiplexer_12_out, multiplexer_13_out, multiplexer_14_out, multiplexer_15_out,
       multiplexer_16_out, multiplexer_18_out, multiplexer_19_out, multiplexer_20_out, multiplexer_21_out,
       register_1_q, register_2_q, register_3_q, register_4_q, register_5_q, register_6_q, register_7_q,
       register_8_q, undriven, undriven_2, undriven_3;

  assign xnor_1_out = ~({8{1'b1}} ^ Register_Select[7:0]);  // XNOR_Gate xnor_1, 8 bits wide
  assign xnor_2_out = ~(8'hfd ^ Register_Select[7:0]);  // XNOR_Gate xnor_2, 8 bits wide
  assign xnor_3_out = ~(8'hfc ^ Register_Select[7:0]);  // XNOR_Gate xnor_3, 8 bits wide
  assign xnor_4_out = ~(8'hfb ^ Register_Select[7:0]);  // XNOR_Gate xnor_4, 8 bits wide
  assign xnor_5_out = ~(8'hfa ^ Register_Select[7:0]);  // XNOR_Gate xnor_5, 8 bits wide
  assign xnor_6_out = ~(8'hf9 ^ Register_Select[7:0]);  // XNOR_Gate xnor_6, 8 bits wide
  assign xnor_7_out = ~(8'hf8 ^ Register_Select[7:0]);  // XNOR_Gate xnor_7, 8 bits wide
  assign xnor_8_out = ~(8'hf7 ^ Register_Select[7:0]);  // XNOR_Gate xnor_8, 8 bits wide
  assign xnor_9_out = ~(8'hf6 ^ Register_Select[7:0]);  // XNOR_Gate xnor_9, 8 bits wide
  assign xnor_10_out = ~(8'hf5 ^ Register_Select[7:0]);  // XNOR_Gate xnor_10, 8 bits wide
  assign xnor_11_out = ~(8'hf4 ^ Register_Select[7:0]);  // XNOR_Gate xnor_11, 8 bits wide
  assign xnor_12_out = ~(8'hf3 ^ Register_Select[7:0]);  // XNOR_Gate xnor_12, 8 bits wide
  assign xnor_13_out = ~(8'hf2 ^ Register_Select[7:0]);  // XNOR_Gate xnor_13, 8 bits wide
  assign xnor_14_out = ~(8'hf1 ^ Register_Select[7:0]);  // XNOR_Gate xnor_14, 8 bits wide
  assign Control_Register_out = ~(Register_Select[11:8] ^ 4'b1111);  // XNOR_Gate Control_Register, 4 bits wide
  assign Plain_Register_out = ~(Register_Select[11:8] ^ 4'b0001);  // XNOR_Gate Plain_Register, 4 bits wide
  assign Arithmetic_Register_out = ~(Register_Select[11:8] ^ 4'b0010);  // XNOR_Gate Arithmetic_Register, 4 bits wide
  and and_1 (and_1_out, and_9_out, xnor_1_out[0], xnor_1_out[1], xnor_1_out[2], xnor_1_out[3], xnor_1_out[4], xnor_1_out[5], xnor_1_out[6], xnor_1_out[7]);
  and and_2 (and_2_out, and_9_out, xnor_3_out[0], xnor_3_out[1], xnor_3_out[2], xnor_3_out[3], xnor_3_out[4], xnor_3_out[5], xnor_3_out[6], xnor_3_out[7]);
  and and_3 (and_3_out, and_9_out, xnor_5_out[0], xnor_5_out[1], xnor_5_out[2], xnor_5_out[3], xnor_5_out[4], xnor_5_out[5], xnor_5_out[6], xnor_5_out[7]);
  and and_4 (and_4_out, and_9_out, xnor_7_out[0], xnor_7_out[1], xnor_7_out[2], xnor_7_out[3], xnor_7_out[4], xnor_7_out[5], xnor_7_out[6], xnor_7_out[7]);
  and and_5 (and_5_out, and_9_out, xnor_9_out[0], xnor_9_out[1], xnor_9_out[2], xnor_9_out[3], xnor_9_out[4], xnor_9_out[5], xnor_9_out[6], xnor_9_out[7]);
  and and_6 (and_6_out, and_9_out, xnor_11_out[0], xnor_11_out[1], xnor_11_out[2], xnor_11_out[3], xnor_11_out[4], xnor_11_out[5], xnor_11_out[6], xnor_11_out[7]);
  and and_7 (and_7_out, and_9_out, xnor_13_out[0], xnor_13_out[1], xnor_13_out[2], xnor_13_out[3], xnor_13_out[4], xnor_13_out[5], xnor_13_out[6], xnor_13_out[7]);
  and and_8 (and_8_out, Control_Register_out[0], Control_Register_out[1], Control_Register_out[2], Control_Register_out[3]);
  and and_9 (and_9_out, Plain_Register_out[0], Plain_Register_out[1], Plain_Register_out[2], Plain_Register_out[3]);
  and and_10 (and_10_out, Arithmetic_Register_out[0], Arithmetic_Register_out[1], Arithmetic_Register_out[2], Arithmetic_Register_out[3]);
  Register #(.width(32)) mdb (.D(Data), .en(and_1_out), .clk(Clock), .Q(mdb_q), .clr(and_11_out));
  and and_11 (and_11_out, Clear, and_1_out);
  Register #(.width(32)) mcd (.D(Data), .en(and_2_out), .clk(Clock), .Q(mcd_q), .clr(and_12_out));
  and and_12 (and_12_out, Clear, and_2_out);
  Register #(.width(32)) mcb (.D(Data), .en(and_3_out), .clk(Clock), .Q(mcb_q), .clr(and_13_out));
  and and_13 (and_13_out, Clear, and_3_out);
  Register #(.width(32)) mbd (.D(Data), .en(and_4_out), .clk(Clock), .Q(mbd_q), .clr(and_14_out));
  and and_14 (and_14_out, Clear, and_4_out);
  Register #(.width(32)) mbb (.D(Data), .en(and_5_out), .clk(Clock), .Q(mbb_q), .clr(and_15_out));
  and and_15 (and_15_out, Clear, and_5_out);
  Register #(.width(32)) mad (.D(Data), .en(and_6_out), .clk(Clock), .Q(mad_q), .clr(and_16_out));
  and and_16 (and_16_out, Clear, and_6_out);
  Register #(.width(32)) mab (.D(Data), .en(and_7_out), .clk(Clock), .Q(mab_q), .clr(and_17_out));
  and and_17 (and_17_out, Clear, and_7_out);
  and and_18 (and_18_out, and_9_out, xnor_2_out[0], xnor_2_out[1], xnor_2_out[2], xnor_2_out[3], xnor_2_out[4], xnor_2_out[5], xnor_2_out[6], xnor_2_out[7]);
  and and_19 (and_19_out, and_9_out, xnor_4_out[0], xnor_4_out[1], xnor_4_out[2], xnor_4_out[3], xnor_4_out[4], xnor_4_out[5], xnor_4_out[6], xnor_4_out[7]);
  and and_20 (and_20_out, and_9_out, xnor_6_out[0], xnor_6_out[1], xnor_6_out[2], xnor_6_out[3], xnor_6_out[4], xnor_6_out[5], xnor_6_out[6], xnor_6_out[7]);
  and and_21 (and_21_out, and_9_out, xnor_8_out[0], xnor_8_out[1], xnor_8_out[2], xnor_8_out[3], xnor_8_out[4], xnor_8_out[5], xnor_8_out[6], xnor_8_out[7]);
  and and_22 (and_22_out, and_9_out, xnor_10_out[0], xnor_10_out[1], xnor_10_out[2], xnor_10_out[3], xnor_10_out[4], xnor_10_out[5], xnor_10_out[6], xnor_10_out[7]);
  and and_23 (and_23_out, and_9_out, xnor_12_out[0], xnor_12_out[1], xnor_12_out[2], xnor_12_out[3], xnor_12_out[4], xnor_12_out[5], xnor_12_out[6], xnor_12_out[7]);
  and and_24 (and_24_out, and_9_out, xnor_14_out[0], xnor_14_out[1], xnor_14_out[2], xnor_14_out[3], xnor_14_out[4], xnor_14_out[5], xnor_14_out[6], xnor_14_out[7]);
  Register #(.width(32)) mda (.D(Data), .en(and_18_out), .clk(Clock), .Q(mda_q), .clr(and_25_out));
  and and_25 (and_25_out, Clear, and_18_out);
  Register #(.width(32)) mcc (.D(Data), .en(and_19_out), .clk(Clear), .Q(mcc_q), .clr(and_26_out));
  and and_26 (and_26_out, Clock, and_19_out);
  Register #(.width(32)) mca (.D(Data), .en(and_20_out), .clk(Clear), .Q(mca_q), .clr(and_27_out));
  and and_27 (and_27_out, Clock, and_20_out);
  Register #(.width(32)) mbc (.D(Data), .en(and_21_out), .clk(Clear), .Q(mbc_q), .clr(and_28_out));
  and and_28 (and_28_out, Clock, and_21_out);
  Register #(.width(32)) mba (.D(Data), .en(and_22_out), .clk(Clear), .Q(mba_q), .clr(and_29_out));
  and and_29 (and_29_out, Clock, and_22_out);
  Register #(.width(32)) mac (.D(Data), .en(and_23_out), .clk(Clear), .Q(mac_q), .clr(and_30_out));
  and and_30 (and_30_out, Clock, and_23_out);
  Register #(.width(32)) maa (.D(Data), .en(and_24_out), .clk(Clear), .Q(maa_q), .clr(and_31_out));
  and and_31 (and_31_out, Clock, and_24_out);
  Multiplexer #(.width(32)) multiplexer_1 (.in0(mdb_q), .in1(mda_q), .out(multiplexer_1_out), .sel(and_18_out));
  Multiplexer #(.width(32)) multiplexer_2 (
    .in0(multiplexer_1_out), .in1(mcd_q), .out(multiplexer_2_out), .sel(and_2_out));
  Multiplexer #(.width(32)) multiplexer_3 (
    .in0(multiplexer_2_out), .in1(mcc_q), .out(multiplexer_3_out), .sel(and_19_out));
  Multiplexer #(.width(32)) multiplexer_4 (
    .in0(multiplexer_3_out), .in1(mcb_q), .out(multiplexer_4_out), .sel(and_3_out));
  Multiplexer #(.width(32)) multiplexer_5 (
    .in0(multiplexer_4_out), .in1(mca_q), .out(multiplexer_5_out), .sel(and_20_out));
  Multiplexer #(.width(32)) multiplexer_6 (
    .in0(multiplexer_5_out), .in1(mbd_q), .out(multiplexer_6_out), .sel(and_4_out));
  Multiplexer #(.width(32)) multiplexer_7 (
    .in0(multiplexer_6_out), .in1(mbc_q), .out(multiplexer_7_out), .sel(and_21_out));
  Multiplexer #(.width(32)) multiplexer_8 (
    .in0(multiplexer_7_out), .in1(mbb_q), .out(multiplexer_8_out), .sel(and_5_out));
  Multiplexer #(.width(32)) multiplexer_9 (
    .in0(multiplexer_8_out), .in1(mba_q), .out(multiplexer_9_out), .sel(and_22_out));
  Multiplexer #(.width(32)) multiplexer_10 (
    .in0(multiplexer_9_out), .in1(mad_q), .out(multiplexer_10_out), .sel(and_6_out));
  Multiplexer #(.width(32)) multiplexer_11 (
    .in0(multiplexer_10_out), .in1(mac_q), .out(multiplexer_11_out), .sel(and_23_out));
  Multiplexer #(.width(32)) multiplexer_12 (
    .in0(multiplexer_11_out), .in1(mab_q), .out(multiplexer_12_out), .sel(and_7_out));
  Multiplexer #(.width(32)) multiplexer_13 (
    .in0(multiplexer_12_out), .in1(maa_q), .out(multiplexer_13_out), .sel(and_24_out));
  assign xnor_15_out = ~({8{1'b1}} ^ Register_Select[7:0]);  // XNOR_Gate xnor_15, 8 bits wide
  assign xnor_16_out = ~(8'hf0 ^ Register_Select[7:0]);  // XNOR_Gate xnor_16, 8 bits wide
  assign xnor_17_out = ~(8'hb0 ^ Register_Select[7:0]);  // XNOR_Gate xnor_17, 8 bits wide
  assign xnor_18_out = ~(8'hb1 ^ Register_Select[7:0]);  // XNOR_Gate xnor_18, 8 bits wide
  assign xnor_19_out = ~({8{1'b0}} ^ Register_Select[7:0]);  // XNOR_Gate xnor_19, 8 bits wide
  assign xnor_20_out = ~(8'h1 ^ Register_Select[7:0]);  // XNOR_Gate xnor_20, 8 bits wide
  assign xnor_21_out = ~(8'h2 ^ Register_Select[7:0]);  // XNOR_Gate xnor_21, 8 bits wide
  assign xnor_22_out = ~(8'h3 ^ Register_Select[7:0]);  // XNOR_Gate xnor_22, 8 bits wide
  // XNOR_Gate xnor_23 has open pins: in0=8'hf4, in1=Register_Select[7:0], out=open
  and and_32 (and_32_out, and_8_out, xnor_15_out[0], xnor_15_out[1], xnor_15_out[2], xnor_15_out[3], xnor_15_out[4], xnor_15_out[5], xnor_15_out[6], xnor_15_out[7]);
  and and_33 (and_33_out, and_8_out, xnor_17_out[0], xnor_17_out[1], xnor_17_out[2], xnor_17_out[3], xnor_17_out[4], xnor_17_out[5], xnor_17_out[6], xnor_17_out[7]);
  Register #(.width(32)) register_1 (.D(Data), .en(and_34_out), .clk(Clear), .Q(register_1_q), .clr(and_35_out));
  and and_34 (and_34_out, and_10_out, xnor_19_out[0], xnor_19_out[1], xnor_19_out[2], xnor_19_out[3], xnor_19_out[4], xnor_19_out[5], xnor_19_out[6], xnor_19_out[7]);
  and and_35 (and_35_out, Clock, and_34_out);
  Register #(.width(32)) register_2 (.D(Data), .en(and_36_out), .clk(Clear), .Q(register_2_q), .clr(and_37_out));
  and and_36 (and_36_out, and_10_out, xnor_21_out[0], xnor_21_out[1], xnor_21_out[2], xnor_21_out[3], xnor_21_out[4], xnor_21_out[5], xnor_21_out[6], xnor_21_out[7]);
  and and_37 (and_37_out, Clock, and_36_out);
  Register #(.width(32)) register_3 (.D(undriven), .en(and_32_out), .clk(Clear), .Q(register_3_q), .clr(and_38_out));
  and and_38 (and_38_out, Clear, and_32_out);
  Register #(.width(32)) register_4 (.D(undriven_2), .en(and_33_out), .clk(Clear), .Q(register_4_q), .clr(and_39_out));
  and and_39 (and_39_out, Clear, and_33_out);
  and and_40 (and_40_out, and_8_out, xnor_16_out[0], xnor_16_out[1], xnor_16_out[2], xnor_16_out[3], xnor_16_out[4], xnor_16_out[5], xnor_16_out[6], xnor_16_out[7]);
  and and_41 (and_41_out, and_8_out, xnor_18_out[0], xnor_18_out[1], xnor_18_out[2], xnor_18_out[3], xnor_18_out[4], xnor_18_out[5], xnor_18_out[6], xnor_18_out[7]);
  Register #(.width(32)) register_5 (.D(Data), .en(and_42_out), .clk(Clear), .Q(register_5_q), .clr(and_43_out));
  and and_42 (and_42_out, and_10_out, xnor_20_out[0], xnor_20_out[1], xnor_20_out[2], xnor_20_out[3], xnor_20_out[4], xnor_20_out[5], xnor_20_out[6], xnor_20_out[7]);
  and and_43 (and_43_out, Clock, and_42_out);
  Register #(.width(32)) register_6 (.D(Data), .en(and_44_out), .clk(Clear), .Q(register_6_q), .clr(and_45_out));
  and and_44 (and_44_out, and_10_out, xnor_22_out[0], xnor_22_out[1], xnor_22_out[2], xnor_22_out[3], xnor_22_out[4], xnor_22_out[5], xnor_22_out[6], xnor_22_out[7]);
  and and_45 (and_45_out, Clock, and_44_out);
  Register #(.width(32)) register_7 (.D(undriven_3), .en(and_40_out), .clk(Clear), .Q(register_7_q), .clr(and_46_out));
  and and_46 (and_46_out, Clear, and_40_out);
  Register #(.width(32)) register_8 (.D(undriven_3), .en(and_41_out), .clk(Clear), .Q(register_8_q), .clr(and_47_out));
  and and_47 (and_47_out, Clear, and_41_out);
  Multiplexer #(.width(32)) multiplexer_14 (
    .in0(multiplexer_21_out), .in1(register_3_q), .out(multiplexer_14_out), .sel(and_32_out));
  Multiplexer #(.width(32)) multiplexer_15 (
    .in0(multiplexer_14_out), .in1(register_7_q), .out(multiplexer_15_out), .sel(and_40_out));
  Multiplexer #(.width(32)) multiplexer_16 (
    .in0(multiplexer_15_out), .in1(register_4_q), .out(multiplexer_16_out), .sel(and_33_out));
  Multiplexer #(.width(32)) multiplexer_17 (
    .in0(multiplexer_16_out), .in1(register_8_q), .out(out_5), .sel(and_41_out));
  Multiplexer #(.width(32)) multiplexer_18 (
    .in0(multiplexer_13_out), .in1(register_1_q), .out(multiplexer_18_out), .sel(and_34_out));
  Multiplexer #(.width(32)) multiplexer_19 (
    .in0(multiplexer_18_out), .in1(register_5_q), .out(multiplexer_19_out), .sel(and_42_out));
  Multiplexer #(.width(32)) multiplexer_20 (
    .in0(multiplexer_19_out), .in1(register_2_q), .out(multiplexer_20_out), .sel(and_36_out));
  Multiplexer #(.width(32)) multiplexer_21 (
    .in0(multiplexer_20_out), .in1(register_6_q), .out(multiplexer_21_out), .sel(and_44_out));
endmodule
